# Fritzing sketch LabsAmbient (saved by Fritzing 0.9.2b)
breadboards: 1

parts:
  Part1 = Arduino Uno (Rev3)
  R1 = PHOTOCELL [package=photocell-kit]
  RHT1 = Humidity and Temperature Sensor RHT03
  T1 = TMP36 Temperature Sensor [thermistor_type=NTC package="TO92 [THT]"]
  R2 = Resistor [tolerance=±5% resistance=10k package=THT]

nets:
  N1: Part1.A0, R1.P$1, R2.Pin_0
  N2: Part1.A1, T1.Vout
  N3: Part1.AREF, Part1.3V3, T1.+Vs
  N4: Part1.D2, RHT1.Data-signal
  5V: Part1.5V, RHT1.Vcc, R2.Pin_1
  GND: Part1.GND, R1.P$2, RHT1.GND_2, T1.GND
